// Logisim project Modified.circ as structural Verilog
module SCDP (
  input  ld
);

  wire ALU_zeroflag, and_1_out, clock_out, Control_alusrc, Control_branch, Control_jump, Control_lwm,
       Control_memread, Control_memtoreg, Control_memwrite, Control_regdst, Control_regwrite;
  wire [1:0] Control_aluop;
  wire [2:0] ALU_Control_alu_operation;
  wire [4:0] multiplexer_1_out;
  wire [27:0] bit_extender_1_out;
  wire [31:0] adder_1_out, ALU_ADD_result, ALU_result, bit_extender_2_out, Data_memory_readdata,
       Instruction_Fetch_Unit_ir, multiplexer_2_out, multiplexer_3_out, multiplexer_4_out, multiplexer_5_out,
       multiplexer_6_out, register_1_q, Register_File_read_data1, Register_File_read_data2;

  Register #(.width(32)) register_1 (.D(multiplexer_4_out), .Q(register_1_q), .clk(clock_out));  // open: en, clr
  Clock clock (.out(clock_out));
  Adder #(.width(32)) adder_1 (.a(register_1_q), .b(32'h1), .out(adder_1_out));  // open: cin, cout
  // Probe on Instruction_Fetch_Unit_ir
  IF Instruction_Fetch_Unit (.in_1(register_1_q), .clock(clock_out), .enable(ld), .IR(Instruction_Fetch_Unit_ir));
  CU Control (
    .opcode(Instruction_Fetch_Unit_ir[31:26]), .RegDst(Control_regdst), .jump(Control_jump),
    .branch(Control_branch), .memRead(Control_memread), .MemToReg(Control_memtoreg), .ALUop(Control_aluop),
    .memWrite(Control_memwrite), .ALUSrc(Control_alusrc), .RegWrite(Control_regwrite), .lwm(Control_lwm));
  assign bit_extender_1_out = {{2{1'b0}}, Instruction_Fetch_Unit_ir[25:0]};  // Bit_Extender bit_extender_1
  Multiplexer #(.width(5), .enable("false")) multiplexer_1 (
    .in0(Instruction_Fetch_Unit_ir[20:16]), .in1(Instruction_Fetch_Unit_ir[15:11]), .out(multiplexer_1_out),
    .sel(Control_regdst));
  assign bit_extender_2_out = {{16{Instruction_Fetch_Unit_ir[15]}}, Instruction_Fetch_Unit_ir[15:0]};  // Bit_Extender bit_extender_2
  ALU ALU_ADD (
    .readData1(adder_1_out), .readData2(bit_extender_2_out), .ALUoperation(3'b010), .result(ALU_ADD_result));  // open: Zeroflag
  RegisterFile Register_File (
    .Read_Reg1(Instruction_Fetch_Unit_ir[25:21]), .clock(clock_out), .Regwrite(Control_regwrite),
    .Write_Reg(multiplexer_1_out), .Write_Data(multiplexer_6_out),
    .Read_Reg2(Instruction_Fetch_Unit_ir[20:16]), .Read_data1(Register_File_read_data1),
    .Read_data2(Register_File_read_data2));
  Multiplexer #(.width(32), .enable("false")) multiplexer_2 (
    .in0(adder_1_out), .in1(ALU_ADD_result), .out(multiplexer_2_out), .sel(and_1_out));
  // Probe on Register_File_read_data1
  Multiplexer #(.width(32), .enable("false")) multiplexer_3 (
    .in0(Register_File_read_data2), .in1(bit_extender_2_out), .out(multiplexer_3_out), .sel(Control_alusrc));
  ALU_control ALU_Control (
    .ALUop(Control_aluop), .Function(Instruction_Fetch_Unit_ir[5:0]),
    .ALU_Operation(ALU_Control_alu_operation));
  ALU ALU (
    .readData1(Register_File_read_data1), .readData2(multiplexer_3_out),
    .ALUoperation(ALU_Control_alu_operation), .Zeroflag(ALU_zeroflag), .result(ALU_result));
  // Probe on multiplexer_3_out
  Multiplexer #(.width(32), .enable("false")) multiplexer_4 (
    .in0(multiplexer_2_out), .in1({adder_1_out[31:28], bit_extender_1_out}), .out(multiplexer_4_out),
    .sel(Control_jump));
  and and_1 (and_1_out, Control_branch, ALU_zeroflag);
  Multiplexer #(.width(32), .enable("false")) multiplexer_5 (
    .in0(ALU_result), .in1(bit_extender_2_out), .out(multiplexer_5_out), .sel(Control_lwm));
  LED jump (.in(Control_jump));
  LED branch (.in(and_1_out));
  Data_Memory Data_memory (
    .Address(multiplexer_5_out), .MemRead(Control_memread), .MemWrite(Control_memwrite),
    .Write_Data(Register_File_read_data2), .clock(clock_out), .ReadData(Data_memory_readdata));
  Multiplexer #(.width(32), .enable("false")) multiplexer_6 (
    .in0(ALU_result), .in1(Data_memory_readdata), .out(multiplexer_6_out), .sel(Control_memtoreg));
  // Probe on multiplexer_6_out

  // Notes on the sheet:
  //   pda
  //   Reg Write
  //   Function
  //   MODIFIED SCDP
  //   Reg dst
  //   BTA
  //   JTA
  //   ALU src
  //   ALU op
  //   branch
  //   jump
  //   lwm
  //   MemRead
  //   MemWrite
  //   MemtoReg
endmodule

module IF (
  input  [31:0] in_1,
  input  clock,
  input  enable,
  output [31:0] IR
);

  RAM #(.addrWidth(24), .dataWidth(32)) ram_1 (
    .addr(in_1[23:0]), .data(IR), .clk(clock), .ld(enable));  // open: sel, clr
endmodule

module RegisterFile (
  input  [4:0] Read_Reg1,
  input  clock,
  input  Regwrite,
  input  [4:0] Write_Reg,
  input  [31:0] Write_Data,
  input  [4:0] Read_Reg2,
  output [31:0] Read_data1,
  output [31:0] Read_data2
);

  wire and_1_out, and_2_out, and_3_out, and_4_out, and_5_out, and_6_out, and_7_out, and_8_out, and_9_out,
       and_10_out, and_11_out, and_12_out, and_13_out, and_14_out, and_15_out, and_16_out, and_17_out,
       and_18_out, and_19_out, and_20_out, and_21_out, and_22_out, and_23_out, and_24_out, and_25_out,
       and_26_out, and_27_out, and_28_out, and_29_out, and_30_out, and_31_out, and_32_out, decoder_1_out0,
       decoder_1_out1, decoder_1_out2, decoder_1_out3, decoder_1_out4, decoder_1_out5, decoder_1_out6,
       decoder_1_out7, decoder_1_out8, decoder_1_out9, decoder_1_out10, decoder_1_out11, decoder_1_out12,
       decoder_1_out13, decoder_1_out14, decoder_1_out15, decoder_1_out16, decoder_1_out17, decoder_1_out18,
       decoder_1_out19, decoder_1_out20, decoder_1_out21, decoder_1_out22, decoder_1_out23, decoder_1_out24,
       decoder_1_out25, decoder_1_out26, decoder_1_out27, decoder_1_out28, decoder_1_out29, decoder_1_out30,
       decoder_1_out31;
  wire [31:0] register_1_q, register_2_q, register_3_q, register_4_q, register_5_q, register_6_q,
       register_7_q, register_8_q, register_9_q, register_10_q, register_11_q, register_12_q, register_13_q,
       register_14_q, register_15_q, register_16_q, register_17_q, register_18_q, register_20_q,
       register_21_q, register_22_q, register_23_q, register_24_q, register_25_q, register_26_q,
       register_27_q, register_28_q, register_29_q, register_30_q, register_31_q;

  Decoder #(.select(5), .enable("false")) decoder_1 (
    .out0(decoder_1_out0), .out1(decoder_1_out1), .out2(decoder_1_out2), .out3(decoder_1_out3),
    .out4(decoder_1_out4), .out5(decoder_1_out5), .out6(decoder_1_out6), .out7(decoder_1_out7),
    .out8(decoder_1_out8), .out9(decoder_1_out9), .out10(decoder_1_out10), .out11(decoder_1_out11),
    .out12(decoder_1_out12), .out13(decoder_1_out13), .out14(decoder_1_out14), .out15(decoder_1_out15),
    .out16(decoder_1_out16), .out17(decoder_1_out17), .out18(decoder_1_out18), .out19(decoder_1_out19),
    .out20(decoder_1_out20), .out21(decoder_1_out21), .out22(decoder_1_out22), .out23(decoder_1_out23),
    .out24(decoder_1_out24), .out25(decoder_1_out25), .out26(decoder_1_out26), .out27(decoder_1_out27),
    .out28(decoder_1_out28), .out29(decoder_1_out29), .out30(decoder_1_out30), .out31(decoder_1_out31),
    .sel(Write_Reg));
  and and_1 (and_1_out, decoder_1_out0, Regwrite);
  and and_2 (and_2_out, decoder_1_out1, Regwrite);
  and and_3 (and_3_out, decoder_1_out2, Regwrite);
  and and_4 (and_4_out, decoder_1_out3, Regwrite);
  and and_5 (and_5_out, decoder_1_out4, Regwrite);
  and and_6 (and_6_out, decoder_1_out5, Regwrite);
  and and_7 (and_7_out, decoder_1_out6, Regwrite);
  and and_8 (and_8_out, decoder_1_out7, Regwrite);
  and and_9 (and_9_out, decoder_1_out8, Regwrite);
  and and_10 (and_10_out, decoder_1_out9, Regwrite);
  and and_11 (and_11_out, decoder_1_out10, Regwrite);
  and and_12 (and_12_out, decoder_1_out11, Regwrite);
  and and_13 (and_13_out, decoder_1_out12, Regwrite);
  and and_14 (and_14_out, decoder_1_out13, Regwrite);
  and and_15 (and_15_out, decoder_1_out14, Regwrite);
  and and_16 (and_16_out, decoder_1_out15, Regwrite);
  and and_17 (and_17_out, decoder_1_out16, Regwrite);
  and and_18 (and_18_out, decoder_1_out17, Regwrite);
  and and_19 (and_19_out, decoder_1_out18, Regwrite);
  and and_20 (and_20_out, decoder_1_out19, Regwrite);
  and and_21 (and_21_out, decoder_1_out20, Regwrite);
  and and_22 (and_22_out, decoder_1_out21, Regwrite);
  and and_23 (and_23_out, decoder_1_out22, Regwrite);
  and and_24 (and_24_out, decoder_1_out23, Regwrite);
  and and_25 (and_25_out, decoder_1_out24, Regwrite);
  and and_26 (and_26_out, decoder_1_out25, Regwrite);
  and and_27 (and_27_out, decoder_1_out26, Regwrite);
  and and_28 (and_28_out, decoder_1_out27, Regwrite);
  and and_29 (and_29_out, decoder_1_out28, Regwrite);
  and and_30 (and_30_out, decoder_1_out29, Regwrite);
  and and_31 (and_31_out, decoder_1_out30, Regwrite);
  and and_32 (and_32_out, decoder_1_out31, Regwrite);
  Register #(.width(32)) register_1 (.D(Write_Data), .en(and_1_out), .Q(register_1_q), .clk(clock));  // open: clr
  Register #(.width(32)) register_2 (.D(Write_Data), .en(and_2_out), .Q(register_2_q), .clk(clock));  // open: clr
  Register #(.width(32)) register_3 (.D(Write_Data), .en(and_3_out), .Q(register_3_q), .clk(clock));  // open: clr
  Register #(.width(32)) register_4 (.D(Write_Data), .en(and_4_out), .Q(register_4_q), .clk(clock));  // open: clr
  Register #(.width(32)) register_5 (.D(Write_Data), .en(and_5_out), .Q(register_5_q), .clk(clock));  // open: clr
  Register #(.width(32)) register_6 (.D(Write_Data), .en(and_6_out), .Q(register_6_q), .clk(clock));  // open: clr
  Register #(.width(32)) register_7 (.D(Write_Data), .en(and_7_out), .Q(register_7_q), .clk(clock));  // open: clr
  Register #(.width(32)) register_8 (.D(Write_Data), .en(and_8_out), .Q(register_8_q), .clk(clock));  // open: clr
  Register #(.width(32)) register_9 (.D(Write_Data), .en(and_9_out), .Q(register_9_q), .clk(clock));  // open: clr
  Register #(.width(32)) register_10 (.D(Write_Data), .en(and_10_out), .Q(register_10_q), .clk(clock));  // open: clr
  Register #(.width(32)) register_11 (.D(Write_Data), .en(and_11_out), .Q(register_11_q), .clk(clock));  // open: clr
  Register #(.width(32)) register_12 (.D(Write_Data), .en(and_12_out), .Q(register_12_q), .clk(clock));  // open: clr
  Register #(.width(32)) register_13 (.D(Write_Data), .en(and_13_out), .Q(register_13_q), .clk(clock));  // open: clr
  Register #(.width(32)) register_14 (.D(Write_Data), .en(and_14_out), .Q(register_14_q), .clk(clock));  // open: clr
  Register #(.width(32)) register_15 (.D(Write_Data), .en(and_15_out), .Q(register_15_q), .clk(clock));  // open: clr
  Register #(.width(32)) register_16 (.D(Write_Data), .en(and_16_out), .Q(register_16_q), .clk(clock));  // open: clr
  Register #(.width(32)) register_17 (.D(Write_Data), .en(and_17_out), .Q(register_17_q), .clk(clock));  // open: clr
  Register #(.width(32)) register_18 (.D(Write_Data), .en(and_18_out), .Q(register_18_q), .clk(clock));  // open: clr
  Register #(.width(32)) register_19 (.D(Write_Data), .en(and_19_out), .Q(register_15_q), .clk(clock));  // open: clr
  Register #(.width(32)) register_20 (.D(Write_Data), .en(and_20_out), .Q(register_20_q), .clk(clock));  // open: clr
  Register #(.width(32)) register_21 (.D(Write_Data), .en(and_21_out), .Q(register_21_q), .clk(clock));  // open: clr
  Register #(.width(32)) register_22 (.D(Write_Data), .en(and_22_out), .Q(register_22_q), .clk(clock));  // open: clr
  Register #(.width(32)) register_23 (.D(Write_Data), .en(and_23_out), .Q(register_23_q), .clk(clock));  // open: clr
  Register #(.width(32)) register_24 (.D(Write_Data), .en(and_24_out), .Q(register_24_q), .clk(clock));  // open: clr
  Register #(.width(32)) register_25 (.D(Write_Data), .en(and_25_out), .Q(register_25_q), .clk(clock));  // open: clr
  Register #(.width(32)) register_26 (.D(Write_Data), .en(and_26_out), .Q(register_26_q), .clk(clock));  // open: clr
  Register #(.width(32)) register_27 (.D(Write_Data), .en(and_27_out), .Q(register_27_q), .clk(clock));  // open: clr
  Register #(.width(32)) register_28 (.D(Write_Data), .en(and_28_out), .Q(register_28_q), .clk(clock));  // open: clr
  Register #(.width(32)) register_29 (.D(Write_Data), .en(and_29_out), .Q(register_29_q), .clk(clock));  // open: clr
  Register #(.width(32)) register_30 (.D(Write_Data), .en(and_30_out), .Q(register_30_q), .clk(clock));  // open: clr
  Register #(.width(32)) register_31 (.D(Write_Data), .en(and_31_out), .Q(register_31_q), .clk(clock));  // open: clr
  Register #(.width(32)) register_32 (.D(Write_Data), .en(and_32_out), .Q(register_15_q), .clk(clock));  // open: clr
  Multiplexer #(.select(5), .width(32)) multiplexer_1 (
    .in0(register_1_q), .in1(register_2_q), .in2(register_3_q), .in3(register_4_q), .in4(register_5_q),
    .in5(register_6_q), .in6(register_7_q), .in7(register_8_q), .in8(register_9_q), .in9(register_10_q),
    .in10(register_11_q), .in11(register_12_q), .in12(register_13_q), .in13(register_14_q),
    .in14(register_15_q), .in15(register_16_q), .in16(register_17_q), .in17(register_18_q),
    .in18(register_15_q), .in19(register_20_q), .in20(register_21_q), .in21(register_22_q),
    .in22(register_23_q), .in23(register_24_q), .in24(register_25_q), .in25(register_26_q),
    .in26(register_27_q), .in27(register_28_q), .in28(register_29_q), .in29(register_30_q),
    .in30(register_31_q), .in31(register_15_q), .out(Read_data1), .sel(Read_Reg1));  // open: en
  Multiplexer #(.select(5), .width(32)) multiplexer_2 (
    .in0(register_1_q), .in1(register_2_q), .in2(register_3_q), .in3(register_4_q), .in4(register_5_q),
    .in5(register_6_q), .in6(register_7_q), .in7(register_8_q), .in8(register_9_q), .in9(register_10_q),
    .in10(register_11_q), .in11(register_12_q), .in12(register_13_q), .in13(register_14_q),
    .in14(register_15_q), .in15(register_16_q), .in16(register_17_q), .in17(register_18_q),
    .in18(register_15_q), .in19(register_20_q), .in20(register_21_q), .in21(register_22_q),
    .in22(register_23_q), .in23(register_24_q), .in24(register_25_q), .in25(register_26_q),
    .in26(register_27_q), .in27(register_28_q), .in28(register_29_q), .in29(register_30_q),
    .in30(register_31_q), .in31(register_15_q), .out(Read_data2), .sel(Read_Reg2));  // open: en
endmodule

module ALU (
  input  [31:0] readData1,
  input  [31:0] readData2,
  input  [2:0] ALUoperation,
  output Zeroflag,
  output [31:0] result
);

  wire subtractor_1_bout;
  wire [31:0] adder_1_out, and_out, bit_extender_1_out, or_out, subtractor_1_out;

  assign and_out = readData1 & readData2;  // AND_Gate and, 32 bits wide
  assign or_out = readData1 | readData2;  // OR_Gate or, 32 bits wide
  Adder #(.width(32)) adder_1 (.a(readData1), .b(readData2), .out(adder_1_out));  // open: cin, cout
  Subtractor #(.width(32)) subtractor_1 (
    .a(readData1), .b(readData2), .out(subtractor_1_out), .bout(subtractor_1_bout));  // open: bin
  assign bit_extender_1_out = {{31{1'b0}}, subtractor_1_bout};  // Bit_Extender bit_extender_1
  Multiplexer #(.select(3), .width(32), .enable("false")) multiplexer_1 (
    .in0(and_out), .in1(or_out), .in2(adder_1_out), .in6(subtractor_1_out), .in7(bit_extender_1_out),
    .out(result), .sel(ALUoperation));  // open: in3, in4, in5
  nor nor_1 (Zeroflag, result[0], result[1], result[2], result[3], result[4], result[5], result[6], result[7], result[8], result[9], result[10], result[11], result[12], result[13], result[14], result[15], result[16], result[17], result[18], result[19], result[20], result[21], result[22], result[23], result[24], result[25], result[26], result[27], result[28], result[29], result[30], result[31]);
endmodule

module ALU_control (
  input  [1:0] ALUop,
  input  [5:0] Function,
  output [2:0] ALU_Operation
);

  wire and_1_out, not_1_out, not_2_out, or_1_out;

  or or_1 (or_1_out, Function[3], Function[0]);
  and and_1 (and_1_out, ALUop[1], Function[1]);
  and and_2 (ALU_Operation[0], ALUop[1], or_1_out);
  not not_1 (not_1_out, ALUop[1]);
  not not_2 (not_2_out, Function[2]);
  or or_2 (ALU_Operation[2], ALUop[0], and_1_out);
  or or_3 (ALU_Operation[1], not_1_out, not_2_out);
endmodule

module Data_Memory (
  input  [31:0] Address,
  input  MemRead,
  input  MemWrite,
  input  [31:0] Write_Data,
  input  clock,
  output [31:0] ReadData
);

  RAM #(.addrWidth(24), .dataWidth(32), .bus("separate")) ram_1 (
    .addr(Address[23:0]), .din(Write_Data), .data(ReadData), .str(MemWrite), .clk(clock), .ld(MemRead));  // open: sel, clr
endmodule

module CU (
  input  [5:0] opcode,
  output RegDst,
  output jump,
  output branch,
  output memRead,
  output MemToReg,
  output [1:0] ALUop,
  output memWrite,
  output ALUSrc,
  output RegWrite,
  output lwm
);

  wire and_1_out, and_2_out, and_4_out, op0_out, op1_out, op2_out, op3_out, op4_out, op5_out, or_1_out;

  not op5 (op5_out, opcode[5]);
  not op4 (op4_out, opcode[4]);
  not op3 (op3_out, opcode[3]);
  not op2 (op2_out, opcode[2]);
  not op0 (op0_out, opcode[0]);
  not op1 (op1_out, opcode[1]);
  and and_1 (and_1_out, op2_out, op1_out);
  and and_2 (and_2_out, op3_out, opcode[5]);
  and and_3 (RegDst, op2_out, op5_out);
  or or_1 (or_1_out, opcode[5], opcode[4]);
  and and_4 (and_4_out, opcode[5], opcode[4]);
  and and_5 (jump, opcode[1], op0_out);
  and and_6 (ALUop[1], op2_out, op1_out);
  and and_7 (lwm, opcode[5], opcode[4]);
  or or_2 (RegWrite, and_1_out, and_2_out);
  and and_8 (memRead, or_1_out, op3_out);
  or or_3 (MemToReg, and_4_out, opcode[0]);

  assign ALUop[0] = opcode[2];
  assign ALUSrc = opcode[0];
  assign branch = opcode[2];
  assign memWrite = opcode[3];
endmodule
